# Fritzing sketch wiring (saved by Fritzing 0.9.3b)
breadboards: 1

parts:
  Teensy1 = Teensy 2.0
  Part1 = Adafruit MCP4725 Breakout Board - 12-Bit DAC [part_number="Adafruit #935"]
  IC1 = IC, DIP package, 8 pins [chip_label=UA741]
  IC2 = IC, DIP package, 8 pins [chip_label=7660s part_number=ICL7660S]
  R1 = Resistor [tolerance=±5% resistance=10k package=THT]
  R2 = Resistor [tolerance=±5% resistance=10k package=THT]
  U1 = BNC socket [package=bnc]
  C1 = Electrolytic Capacitor [capacitance=10µF package="100 mil [THT, electrolytic]"]
  C2 = Electrolytic Capacitor [capacitance=10µF package="100 mil [THT, electrolytic]"]
  U3 = Voltage Regulator - 5V [package="TO220 [THT]"]
  Power_12V = Power plug
  C3 = Tantalum Capacitor [capacitance=1µF package="100 mil [THT, tantalum]"]
  R4 = TRIMPOT [package=3362u-2]
  U4 = BNC socket [package=bnc]
  U5 = BNC socket [package=bnc]
  R5 = Resistor [tolerance=±5% resistance=1k package=THT]
  R6 = Resistor [tolerance=±5% resistance=1k package=THT]
  U6 = BNC socket [package=bnc]
  R7 = TRIMPOT [package=3362u-2]
  IC3 = IC, DIP package, 8 pins [chip_label=UA741 part_number="Summing opAmp"]
  R8 = Resistor [tolerance=±5% resistance=1k package=THT]
  R9 = Resistor [tolerance=±5% resistance=1k package=THT]

nets (from the schematic view):
  GND: Teensy1.GND, Part1.GND, IC2.pin3, C2.+, U3.GND, Power_12V.GND, C3.-, R4.WIPER, R7.WIPER, R8.Pin_0
  N1: Teensy1.D0, Part1.SCL
  N2: Teensy1.D1, Part1.SDA
  N3: Teensy1.D2, U1.OUT
  5V: Part1.VDD, IC1.pin7, IC2.pin8, R1.Pin_1, U3.output_voltage, IC3.pin7
  N4: Part1.VOUT, IC1.pin3
  N5: IC1.pin1, R4.CCW
  N6: IC1.pin2, R1.Pin_0, R2.Pin_0
  N7: IC1.pin4, IC2.pin5, C2.-, IC3.pin4
  N8: IC1.pin5, R4.CW
  N9: IC1.pin6, R2.Pin_1, R6.Pin_0, U6.OUT
  N10: IC2.pin2, C1.+
  N11: IC2.pin4, C1.-
  N12: U3.input_voltage, Power_12V.VCC, C3.+
  N13: U4.OUT, R5.Pin_0
  N14: U5.OUT, IC3.pin6, R9.Pin_1
  N15: R5.Pin_1, R6.Pin_1, IC3.pin3
  N16: R7.CCW, IC3.pin1
  N17: R7.CW, IC3.pin5
  N18: IC3.pin2, R8.Pin_1, R9.Pin_0

notes:
  opAmp
  12 bit DAC

custom parts:
  Adafruit MCP4725 Breakout Board - 12-Bit DAC: Your microcontroller probably has an ADC (analog -> digital converter) but does it have a DAC (digital -> analog converter)??? Now it can! This breakout board features the easy-to-use MCP4725 12-bit DAC. Control it via I2C and send it the value you want it to output, and the VOUT pin will have it. Great for audio / analog projects, such as when you can't use PWM but need a sine wave or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
